// Logisim project ISA.circ as structural Verilog: 3 circuits, main circuit ULA
module Main (
);

  wire and_1_out, Branch, comparator_1_eq, Mem_read, Mem_write, MemToReg, RegWrite, ula_1_zero, ULAsrc;
  wire [1:0] FUNCT, RD, RS1, RS2;
  wire [3:0] Funct_data, IMM, multiplexer_3_out, OPCODE, ULA_CONTROL;
  wire [5:0] MINS_data;
  wire [11:0] adder_1_out, b_reg_1_saida_1, b_reg_1_saida_2, bit_extender_1_out, multiplexer_1_out,
       multiplexer_2_out, multiplexer_4_out, PC_q, ula_1_saida;

  Multiplexer #(.width(12)) multiplexer_1 (.in0(adder_1_out), .out(multiplexer_1_out), .sel(and_1_out));  // open: in1
  Register #(.width(12)) PC (.D(multiplexer_1_out), .Q(PC_q));  // open: en, clk, clr
  Adder #(.width(12)) adder_1 (.a(PC_q), .b(12'h1), .out(adder_1_out));  // open: cin, cout
  ROM #(.addrWidth(12), .dataWidth(12)) MINS (.addr(PC_q), .data({OPCODE, RD, MINS_data}));
  ROM #(.addrWidth(4), .dataWidth(10)) UCONTROL (
    .addr(OPCODE), .data({RegWrite, ULA_CONTROL, ULAsrc, Mem_read, Mem_write, MemToReg, Branch}));
  assign bit_extender_1_out = {{8{IMM[3]}}, IMM};  // Bit_Extender bit_extender_1
  B_REG b_reg_1 (
    .DATA(multiplexer_4_out), .RegWrite(RegWrite), .RD(RD), .RS1(RS1), .RS2(RS2), .SAIDA_1(b_reg_1_saida_1),
    .SAIDA_2(b_reg_1_saida_2));  // open: CLK
  RAM #(.addrWidth(12), .dataWidth(12)) MDATA (
    .addr(ula_1_saida), .we(Mem_write), .oe(Mem_read), .din(b_reg_1_saida_2), .dout(b_reg_1_saida_2));  // open: clk
  Multiplexer #(.width(12)) multiplexer_2 (
    .in0(b_reg_1_saida_2), .in1(bit_extender_1_out), .out(multiplexer_2_out), .sel(ULAsrc));
  Multiplexer #(.width(4)) multiplexer_3 (
    .in0(ULA_CONTROL), .in1(Funct_data), .out(multiplexer_3_out), .sel(comparator_1_eq));
  Comparator #(.width(4)) comparator_1 (.a(ULA_CONTROL), .b(4'b0111), .eq(comparator_1_eq));  // open: gt, lt
  ULA ula_1 (
    .rs1(b_reg_1_saida_1), .rs2(multiplexer_2_out), .ULA_CONTROL(multiplexer_3_out), .ZERO(ula_1_zero),
    .SAIDA(ula_1_saida));
  ROM #(.addrWidth(2), .dataWidth(4)) u_Funct (.addr(FUNCT), .data(Funct_data));
  Multiplexer #(.width(12)) multiplexer_4 (
    .in0(ula_1_saida), .in1(b_reg_1_saida_2), .out(multiplexer_4_out), .sel(MemToReg));
  // AND_Gate and_1 has open pins: out=and_1_out

  // Notes on the sheet:
  //   contents of UCONTROL (hex, n*v repeats v):
  //   3e0 250 2f0 210 230 270 310 330 25a 54 c1 c1 251 0 0 201
  //   contents of Funct (hex, n*v repeats v):
  //   2 6 0 7
endmodule

module ULA (
  input  [11:0] rs1,
  input  [11:0] rs2,
  input  [3:0] ULA_CONTROL,
  output ZERO,
  output [11:0] SAIDA
);

  wire comparator_1_lt;
  wire [11:0] adder_1_out, and_1_out, bit_extender_1_out, multiplexer_1_out, not_1_out, or_1_out,
       shifter_1_out, shifter_2_out, subtractor_1_out, xor_1_out;

  Adder #(.width(12)) adder_1 (.a(rs1), .b(rs2), .out(adder_1_out));  // open: cin, cout
  Subtractor #(.width(12)) subtractor_1 (.a(rs1), .b(rs2), .out(subtractor_1_out));  // open: bin, bout
  Shifter #(.width(12)) shifter_1 (.in(rs1), .\dist (4'b0001), .out(shifter_1_out));
  Shifter #(.shift("lr"), .width(12)) shifter_2 (.in(rs1), .\dist (4'b0001), .out(shifter_2_out));
  assign and_1_out = rs1 & rs2;  // AND_Gate and_1, 12 bits wide
  assign or_1_out = rs1 | rs2;  // OR_Gate or_1, 12 bits wide
  assign xor_1_out = rs1 ^ rs2;  // XOR_Gate xor_1, 12 bits wide
  assign not_1_out = ~rs1;  // NOT_Gate not_1, 12 bits wide
  Comparator #(.width(12)) comparator_1 (.a(rs1), .b(rs2), .lt(comparator_1_lt));  // open: gt, eq
  assign bit_extender_1_out = {{11{comparator_1_lt}}, comparator_1_lt};  // Bit_Extender bit_extender_1
  Multiplexer #(.select(4), .width(12)) multiplexer_1 (
    .in0(adder_1_out), .in1(subtractor_1_out), .in2(shifter_1_out), .in3(shifter_2_out), .in4(and_1_out),
    .in5(or_1_out), .in6(xor_1_out), .in7(not_1_out), .in8(bit_extender_1_out), .out(multiplexer_1_out),
    .sel(ULA_CONTROL));  // open: in9, in10, in11, in12, in13, in14, in15
  nor nor_1 (ZERO, multiplexer_1_out[0], multiplexer_1_out[1], multiplexer_1_out[2], multiplexer_1_out[3], multiplexer_1_out[4], multiplexer_1_out[5], multiplexer_1_out[6], multiplexer_1_out[7], multiplexer_1_out[8], multiplexer_1_out[9], multiplexer_1_out[10], multiplexer_1_out[11]);
endmodule

module B_REG (
  input  [11:0] DATA,
  input  RegWrite,
  input  CLK,
  input  [1:0] RD,
  input  [1:0] RS1,
  input  [1:0] RS2,
  output [11:0] SAIDA_1,
  output [11:0] SAIDA_2
);

  wire and_1_out, and_2_out, and_3_out, and_4_out, decoder_1_out0, decoder_1_out1, decoder_1_out2,
       decoder_1_out3;
  wire [11:0] R0, R1, R2, R3, undriven;

  Decoder #(.select(2)) decoder_1 (
    .out0(decoder_1_out0), .out1(decoder_1_out1), .out2(decoder_1_out2), .out3(decoder_1_out3), .sel(RD));  // open: en
  and and_1 (and_1_out, decoder_1_out0, RegWrite);
  and and_2 (and_2_out, decoder_1_out3, RegWrite);
  and and_3 (and_3_out, decoder_1_out1, RegWrite);
  and and_4 (and_4_out, decoder_1_out2, RegWrite);
  Register #(.width(12)) register_1 (.D(undriven), .en(and_1_out), .Q(R0));  // open: clk, clr
  Register #(.width(12)) register_2 (.D(undriven), .en(and_4_out), .Q(R2));  // open: clk, clr
  Register #(.width(12)) register_3 (.D(undriven), .en(and_3_out), .Q(R1));  // open: clk, clr
  Register #(.width(12)) register_4 (.D(undriven), .en(and_2_out), .Q(R3));  // open: clk, clr
  Multiplexer #(.select(2), .width(12)) multiplexer_1 (
    .in0(R0), .in1(R1), .in2(R2), .in3(R3), .out(SAIDA_1), .sel(RS1));
  Multiplexer #(.select(2), .width(12)) multiplexer_2 (
    .in0(R0), .in1(R1), .in2(R2), .in3(R3), .out(SAIDA_2), .sel(RS2));
endmodule
